# Fritzing sketch circuit_layout (saved by Fritzing 0.9.4)
breadboards: 1

parts:
  Part1 = Arduino Uno (Rev3)
  LCD1 = Adafruit Positive RGB 2x16 LCD
  microSD1 = MicroSD Card Module  # not connected
  R1 = Rotary Potentiometer (Small) [maximum_resistance=100kΩ package=THT]
  S2 = Pushbutton [package="[THT]"]
  S3 = Pushbutton [package="[THT]"]
  S4 = Pushbutton [package="[THT]"]
  R2 = Resistor [tolerance=±5% resistance=10k package=THT]
  R3 = Resistor [tolerance=±5% resistance=10k package=THT]
  R4 = Resistor [tolerance=±5% resistance=10k package=THT]

nets:
  N1: Part1.A1, S3.Pin_1, R4.Pin_1
  N2: Part1.A2, S2.Pin_1, S2.Pin_2, R3.Pin_1
  N3: Part1.A3, S4.Pin_1, S4.Pin_2, R2.Pin_1
  N4: Part1.A4/SDA, LCD1.no_name_yet#3
  N5: Part1.D8, LCD1.no_name_yet#13
  N6: Part1.D9_PWM, LCD1.no_name_yet#17
  N7: Part1.D2, LCD1.no_name_yet#5
  N8: Part1.D3_PWM, LCD1.no_name_yet#15
  N9: Part1.D4, LCD1.no_name_yet#12
  N10: Part1.D5_PWM, LCD1.no_name_yet#16
  N11: Part1.D6_PWM, LCD1.no_name_yet#10
  N12: Part1.D7, LCD1.no_name_yet#11
  N13: Part1.5V, LCD1.no_name_yet#1, LCD1.no_name_yet#14, R1.leg1, S2.Pin_3, S2.Pin_4, S3.Pin_3, S4.Pin_3, S4.Pin_4
  N14: Part1.GND, LCD1.no_name_yet#0, LCD1.no_name_yet#4, R1.leg2, R2.Pin_0, R3.Pin_0, R4.Pin_0
  N15: LCD1.no_name_yet#2, R1.wiper

custom parts:
  Adafruit Positive RGB 2x16 LCD: Adafruit Positive 2x16 LCD Display with RGB Backlight
